# Fritzing sketch CircuitDiagram (saved by Fritzing 0.9.3b)
breadboards: 1

parts:
  Part1 = Arduino Uno (Rev3) - ICSP
  LED2 = smd LED [color="Red (633nm)" package="0603 [SMD]"]
  LED3 = smd LED [color="Green (570nm)" package="1206 [SMD]"]
  LED3_2 = smd LED [color="Green (570nm)" package="1206 [SMD]"]
  R3 = Resistor [tolerance=±5% resistance=220 package="2512 [SMD]"]
  LED6 = smd LED [color="Green (570nm)" package="1206 [SMD]"]
  S5 = Momentary Switch [package=ksa_sealed_tac_switch]
  R10 = Resistor [tolerance=±5% resistance=10k package="2512 [SMD]"]
  R13 = Rotary Potentiometer (Small) [maximum_resistance=100kΩ package=THT]
  hc-sr1 = hc-sr04  # not connected
  R14 = PHOTOCELL [package=photocell]
  R15 = Resistor [tolerance=±5% resistance=10k package="2512 [SMD]"]
  R11 = Resistor [tolerance=±5% resistance=220 package="2512 [SMD]"]
  R16 = Resistor [tolerance=±5% resistance=220 package="2512 [SMD]"]
  J1 = Infrared Proximity Sensor
  LCD1 = LCD screen
  LCM1602_IIC1 = LCM1602 IIC [part_number="LCM1602 IIC" chip_label="LCM1602 IIC" package="DIP (Dual Inline) [THT]"]
  J2 = Basic Servo  # not connected

nets:
  N1: Part1.A0, R14.P$1, R15.Pin_0
  N2: Part1.A1, R13.wiper
  N3: Part1.A4/SDA, LCM1602_IIC1.SCL
  N4: Part1.A5/SCL, LCM1602_IIC1.SDA
  N5: Part1.D2, J1.Vout
  N6: Part1.D3_PWM, LED3.anode, LED3_2.anode
  N7: Part1.D4, LED6.anode
  N8: Part1.D5_PWM, LED2.anode
  N9: Part1.D6_PWM, S5.4, R10.Pin_0
  VCC: Part1.5V, R13.leg2, R14.P$2, J1.Vcc, LCM1602_IIC1.VCC
  GND: Part1.GND, R3.Pin_1, R10.Pin_1, R13.leg1, R15.Pin_1, R11.Pin_1, R16.Pin_1, J1.GND, LCM1602_IIC1.GND
  N10: LED2.cathode, R11.Pin_0
  N11: LED3.cathode, LED3_2.cathode, R3.Pin_0
  N12: LED6.cathode, R16.Pin_0
  VSS: LCD1.VSS, LCM1602_IIC1.VSS
  VDD: LCD1.VDD, LCM1602_IIC1.VDD
  N13: LCD1.V0, LCM1602_IIC1.V0
  N14: LCD1.RS, LCM1602_IIC1.RS
  N15: LCD1.R/W, LCM1602_IIC1.RW
  N16: LCD1.E, LCM1602_IIC1.E
  N17: LCD1.DB0, LCM1602_IIC1.D0
  N18: LCD1.DB1, LCM1602_IIC1.D1
  N19: LCD1.DB2, LCM1602_IIC1.D2
  N20: LCD1.DB3, LCM1602_IIC1.D3
  N21: LCD1.DB4, LCM1602_IIC1.D4
  N22: LCD1.DB5, LCM1602_IIC1.D5
  N23: LCD1.DB6, LCM1602_IIC1.D6
  N24: LCD1.DB7, LCM1602_IIC1.D7
  N25: LCD1.LED+, LCD1.LED-, LCM1602_IIC1.A, LCM1602_IIC1.K
  N26: LCM1602_IIC1.LED_A, LCM1602_IIC1.LED_B

custom parts:
  LCM1602 IIC: I2C-Module to use a 1602 or 2004 LCD on with the wire.h libory Serial LCD Modul
